# Fritzing sketch avr_swd_to_jtag_and_isp_mapping (saved by Fritzing 1.0.6)
breadboards: 1

parts:
  SWD_Debug/Program = Adafruit 2x5 SWD Breakout [part_number="Adafruit #2743"]
  Part1 = Arduino Uno (Rev3) - ICSP
  ISCP_Program1 = Adafruit AVR 6-ISP Breakout [part_number="Adafruit #1465"]

nets:
  GND: SWD_Debug/Program.SWIO, SWD_Debug/Program.RESET, Part1.GND, ISCP_Program1.GND
  5V: SWD_Debug/Program.CLK, Part1.5V, ISCP_Program1.VCC
  N1: SWD_Debug/Program.SWO, SWD_Debug/Program.NC, Part1.RESET
  N2: SWD_Debug/Program.VREF, Part1.ICSP_SCK, Part1.D13/SCK, ISCP_Program1.SCK
  N3: SWD_Debug/Program.GND, Part1.ICSP_MISO, Part1.D12/MISO, ISCP_Program1.MISO
  N4: SWD_Debug/Program.GNDD, Part1.ICSP_MOSI, Part1.D11_PWM/MOSI, ISCP_Program1.MOSI

notes:
  TCK
  TDO
  TMS
  TDI
  MOSI/COPI
  RST
  MISO/CIPO
  SCK
  CLK = 5V
  SWO = RST
  SWIO = GND
  !RST = GND
  NC = RST
  GNDd = TDI
  KEY = NC
  GND2 = TMS
  GND1 = TDO
  GND1 = MISO (CIPO)
  GNDd = MOSI (COPI)
  Vref = SCK
  SWD to ISP Mapping
  SWD to JTAG Mapping
  Vref = TCK
  5V
  GND
  MISO
  MOSI
  Mega 2560
  A7 = TDI
  A5 = TMS
  A6 = TDO
  A4 = TCK
  UNO
  1 = MISO (CIPO)
  5 = RST
  6 =GND
  4 = MOSI (COPI)
  2 = 5V
  3 = SCK
  A0 = TDI
  A2 = TMS
  A1 = TDO
  Micro
  A3 = TCK
  D14 = MISO (CIPO)
  D16 = MOSI (COPI)
  D15 = SCK
  Pro Micro
  JTAG
  ISP
  1/D50 = MISO (CIPO)
  4/D51 = MOSI (COPI)
  3/D52 = SCK

custom parts:
  Adafruit 2x5 SWD Breakout: This adapter board is designed to make it easier to use ARM dev boards that use slimmer 2x5 (0.05"/1.27mm pitch) SWD cables for programming. It's helpful for using products like the JTAGulator, STLink or SEGGER J-Link with tiny boards that use the 10-pin SWD programming connector, often Cortex M0 or M3's. This board comes with no cables. It's really just the breakout board and some header if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
  Adafruit AVR 6-ISP Breakout: Programming AVR? Always Googling the pinout? Well, now no longer! It's rare to find a mini kit so elegant, it deserves its own Haiku. A simple breakout, 2x3 box header in the center, two 1x3's on the side. Plugs into any breadboard for neat wiring (in both nifty and clean senses of the word). Comes with a quality mini PCB, a 2x3 box header and a small stick of 0.1" header. Requires some light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
