# Fritzing sketch micro_program_debug (saved by Fritzing 1.0.6)
breadboards: 1

parts:
  ISCP_Program = Adafruit AVR 6-ISP Breakout [part_number="Adafruit #1465"]
  SWD_to_JTAG_Debug = Adafruit 2x5 SWD Breakout [part_number="Adafruit #2743"]
  Part1 = Arduino Micro (Rev3)
  S1 = Pushbutton [package="[THT]"]
  P3022-V1-CW360 = ENCODER-QUADRATURE [package=encoder-16mm-quad]

nets:
  N1: ISCP_Program.RST, SWD_to_JTAG_Debug.SWO, SWD_to_JTAG_Debug.NC, Part1.RESET, S1.Pin_3, S1.Pin_4
  VCC: ISCP_Program.VCC, SWD_to_JTAG_Debug.CLK, Part1.5V, P3022-V1-CW360.C
  GND: ISCP_Program.GND, SWD_to_JTAG_Debug.SWIO, SWD_to_JTAG_Debug.RESET, Part1.GND, S1.Pin_1, S1.Pin_2, P3022-V1-CW360.A
  N2: SWD_to_JTAG_Debug.VREF, Part1.A3
  N3: SWD_to_JTAG_Debug.GND, Part1.A1
  N4: SWD_to_JTAG_Debug.GND2, Part1.A2
  N5: SWD_to_JTAG_Debug.GNDD, Part1.A0
  N6: Part1.D10_PWM/A10, P3022-V1-CW360.B

notes:
  TCK
  TDO
  TMS
  TDI
  Vref = TCK
  GND1 = TDO
  GND2 = TMS
  KEY = NC
  GNDd = TDI
  NC = RST
  !RST = GND
  SWIO = GND
  SWO = RST
  CLK = 5V
  RST
  A10
  MOSI
  MISO
  SCK
  5V
  GND

custom parts:
  Adafruit AVR 6-ISP Breakout: Programming AVR? Always Googling the pinout? Well, now no longer! It's rare to find a mini kit so elegant, it deserves its own Haiku. A simple breakout, 2x3 box header in the center, two 1x3's on the side. Plugs into any breadboard for neat wiring (in both nifty and clean senses of the word). Comes with a quality mini PCB, a 2x3 box header and a small stick of 0.1" header. Requires some light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
  Adafruit 2x5 SWD Breakout: This adapter board is designed to make it easier to use ARM dev boards that use slimmer 2x5 (0.05"/1.27mm pitch) SWD cables for programming. It's helpful for using products like the JTAGulator, STLink or SEGGER J-Link with tiny boards that use the 10-pin SWD programming connector, often Cortex M0 or M3's. This board comes with no cables. It's really just the breakout board and some header if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
