# Fritzing sketch micro_swd_to_jtag_and_isp_mapping (saved by Fritzing 1.0.6)
breadboards: 1

parts:
  Part1 = Arduino Micro (Rev3)
  S1 = Pushbutton [package="[THT]"]
  P3022-V1-CW360 = ENCODER-QUADRATURE [package=encoder-16mm-quad]
  SWD_Debug/Program = Adafruit 2x5 SWD Breakout [part_number="Adafruit #2743"]

nets:
  N1: Part1.MOSI, Part1.A0, SWD_Debug/Program.GNDD
  N2: Part1.RESET, S1.Pin_3, S1.Pin_4, SWD_Debug/Program.SWO, SWD_Debug/Program.NC
  N3: Part1.GND, P3022-V1-CW360.A, SWD_Debug/Program.SWIO, SWD_Debug/Program.RESET
  N4: Part1.D10_PWM/A10, P3022-V1-CW360.B
  N5: Part1.SCK, Part1.A3, SWD_Debug/Program.VREF
  N6: Part1.MISO, Part1.A1, SWD_Debug/Program.GND
  N7: Part1.5V, S1.Pin_1, S1.Pin_2, P3022-V1-CW360.C, SWD_Debug/Program.CLK
  N8: Part1.A2, SWD_Debug/Program.GND2

notes:
  TCK
  TDO
  TMS
  TDI
  RST
  A10
  MOSI
  MISO
  SCK
  CLK = 5V
  SWO = RST
  SWIO = GND
  !RST = GND
  NC = RST
  GNDd = TDI = A0
  KEY = NC
  GND2 = TMS = A2
  GND1 = TDO = A1
  GND1 = MISO
  GNDd = MOSI
  Vref = SCK
  SWD to ISP Mapping
  SWD to JTAG Mapping
  Vref = TCK = A3
  5V
  GND

custom parts:
  Adafruit 2x5 SWD Breakout: This adapter board is designed to make it easier to use ARM dev boards that use slimmer 2x5 (0.05"/1.27mm pitch) SWD cables for programming. It's helpful for using products like the JTAGulator, STLink or SEGGER J-Link with tiny boards that use the 10-pin SWD programming connector, often Cortex M0 or M3's. This board comes with no cables. It's really just the breakout board and some header if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
