# Fritzing sketch promicro_production (saved by Fritzing 1.0.6)

parts:
  P3022-V1-CW361 = ENCODER-QUADRATURE [package=encoder-16mm-quad]
  Promicro = Pro Micro

nets:
  N1: P3022-V1-CW361.A, Promicro.GND
  N2: P3022-V1-CW361.B, Promicro.D10
  N3: P3022-V1-CW361.C, Promicro.VCC

custom parts:
  Pro Micro: The SparkFun Pro Micro is a complete USB-based microcontoller development system, in a very small footprint, capable of implementing many types of projects. All programming can be done via the USB port.
