# Fritzing sketch promicro_program_debug (saved by Fritzing 1.0.6)
breadboards: 1

parts:
  ISCP_Program = Adafruit AVR 6-ISP Breakout [part_number="Adafruit #1465"]
  SWD_to_JTAG_Debug/Program = Adafruit 2x5 SWD Breakout [part_number="Adafruit #2743"]
  S1 = Pushbutton [package="[THT]"]
  Pro_Micro1 = Pro Micro
  P3022-V1-CW360 = ENCODER-QUADRATURE [package=encoder-16mm-quad]

nets:
  VCC: ISCP_Program.VCC, SWD_to_JTAG_Debug/Program.CLK, Pro_Micro1.VCC, P3022-V1-CW360.C
  N1: ISCP_Program.MOSI, Pro_Micro1.D16/MOSI
  N2: ISCP_Program.RST, SWD_to_JTAG_Debug/Program.SWO, SWD_to_JTAG_Debug/Program.NC, S1.Pin_3, S1.Pin_4, Pro_Micro1.RST
  GND: ISCP_Program.GND, SWD_to_JTAG_Debug/Program.SWIO, SWD_to_JTAG_Debug/Program.RESET, S1.Pin_1, S1.Pin_2, Pro_Micro1.GND, P3022-V1-CW360.A
  N3: ISCP_Program.SCK, Pro_Micro1.D15/SCLK
  N4: ISCP_Program.MISO, Pro_Micro1.D14/MISO
  N5: SWD_to_JTAG_Debug/Program.VREF, Pro_Micro1.D21/A3
  N6: SWD_to_JTAG_Debug/Program.GND, Pro_Micro1.D19/A1
  N7: SWD_to_JTAG_Debug/Program.GND2, Pro_Micro1.D20/A2
  N8: SWD_to_JTAG_Debug/Program.GNDD, Pro_Micro1.D18/A0
  N9: Pro_Micro1.D10, P3022-V1-CW360.B

notes:
  TCK
  TDO
  TMS
  TDI
  Vref = TCK = A3
  GND1 = TDO = A1
  GND2 = TMS = A2
  KEY = NC
  GNDd = TDI = A0
  NC = RST
  !RST = GND
  SWIO = GND
  SWO = RST
  CLK = 5V
  A10
  SCK
  MISO
  MOSI
  MISO = 14
  SCK = 15
  RST = RST
  VCC = VCC
  MOSI = 16
  GND = GND

custom parts:
  Adafruit AVR 6-ISP Breakout: Programming AVR? Always Googling the pinout? Well, now no longer! It's rare to find a mini kit so elegant, it deserves its own Haiku. A simple breakout, 2x3 box header in the center, two 1x3's on the side. Plugs into any breadboard for neat wiring (in both nifty and clean senses of the word). Comes with a quality mini PCB, a 2x3 box header and a small stick of 0.1" header. Requires some light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
  Adafruit 2x5 SWD Breakout: This adapter board is designed to make it easier to use ARM dev boards that use slimmer 2x5 (0.05"/1.27mm pitch) SWD cables for programming. It's helpful for using products like the JTAGulator, STLink or SEGGER J-Link with tiny boards that use the 10-pin SWD programming connector, often Cortex M0 or M3's. This board comes with no cables. It's really just the breakout board and some header if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
  Pro Micro: The SparkFun Pro Micro is a complete USB-based microcontoller development system, in a very small footprint, capable of implementing many types of projects. All programming can be done via the USB port.
