# Fritzing sketch promicro_swd_to_jtag_and_isp_mapping (saved by Fritzing 1.0.6)
breadboards: 1

parts:
  SWD_Debug/Program = Adafruit 2x5 SWD Breakout [part_number="Adafruit #2743"]
  Pro_Micro2 = Pro Micro
  P3022-V1-CW360 = ENCODER-QUADRATURE [package=encoder-16mm-quad]
  S1 = Pushbutton [package="[THT]"]

nets:
  N1: SWD_Debug/Program.SWIO, SWD_Debug/Program.RESET, Pro_Micro2.GND, P3022-V1-CW360.A, S1.Pin_1, S1.Pin_2
  N2: SWD_Debug/Program.CLK, Pro_Micro2.VCC, P3022-V1-CW360.C
  N3: SWD_Debug/Program.SWO, SWD_Debug/Program.NC, Pro_Micro2.RST, S1.Pin_3, S1.Pin_4
  N4: SWD_Debug/Program.VREF, Pro_Micro2.D15/SCLK, Pro_Micro2.D21/A3
  N5: SWD_Debug/Program.GND, Pro_Micro2.D14/MISO, Pro_Micro2.D19/A1
  N6: SWD_Debug/Program.GND2, Pro_Micro2.D20/A2
  N7: SWD_Debug/Program.GNDD, Pro_Micro2.D16/MOSI, Pro_Micro2.D18/A0
  N8: Pro_Micro2.D10, P3022-V1-CW360.B

notes:
  TCK
  TDO
  TMS
  TDI
  Vref = TCK = A3
  GND1 = TDO = A1
  GND2 = TMS = A2
  KEY = NC
  GNDd = TDI = A0
  NC = RST
  !RST = GND
  SWIO = GND
  SWO = RST
  CLK = 5V
  SCK
  MISO
  MOSI
  Vref = SCK = 15
  GNDd = MOSI = 16
  GND1 = MISO = 14
  SWD to JTAG Mapping
  SWD to ISP Mapping

custom parts:
  Adafruit 2x5 SWD Breakout: This adapter board is designed to make it easier to use ARM dev boards that use slimmer 2x5 (0.05"/1.27mm pitch) SWD cables for programming. It's helpful for using products like the JTAGulator, STLink or SEGGER J-Link with tiny boards that use the 10-pin SWD programming connector, often Cortex M0 or M3's. This board comes with no cables. It's really just the breakout board and some header if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
  Pro Micro: The SparkFun Pro Micro is a complete USB-based microcontoller development system, in a very small footprint, capable of implementing many types of projects. All programming can be done via the USB port.
